// Logisim project master.circ as structural Verilog: 20 circuits, main circuit FullAdder
module HalfAdder (
  input  A,
  input  B,
  output Sum,
  output Cout
);

  xor xor_1 (Sum, A, B);
  and and_1 (Cout, A, B);
endmodule

module FullAdder (
  input  A,
  input  B,
  input  Cin,
  output Sum,
  output Cout
);

  wire and_1_out, and_2_out, and_3_out, xor_1_out;

  and and_1 (and_1_out, B, Cin);
  and and_2 (and_2_out, A, Cin);
  and and_3 (and_3_out, A, B);
  or or_1 (Cout, and_1_out, and_2_out, and_3_out);
  xor xor_1 (xor_1_out, A, B);
  xor xor_2 (Sum, xor_1_out, Cin);
endmodule

module FullSubtractor (
  input  A,
  input  B,
  input  Bin,
  output Sum,
  output Bout
);

  wire and_1_out, and_2_out, and_3_out, not_1_out, not_2_out, xor_1_out;

  and and_1 (and_1_out, B, Bin);
  not not_1 (not_1_out, A);
  and and_2 (and_2_out, not_1_out, Bin);
  not not_2 (not_2_out, A);
  and and_3 (and_3_out, not_2_out, B);
  or or_1 (Bout, and_1_out, and_2_out, and_3_out);
  xor xor_1 (xor_1_out, A, B);
  xor xor_2 (Sum, xor_1_out, Bin);
endmodule

module OnesComp (
  input  [3:0] A,
  output [3:0] R
);

  not not_1 (R[0], A[0]);
  not not_2 (R[1], A[1]);
  not not_3 (R[2], A[2]);
  not not_4 (R[3], A[3]);
endmodule

module TwosComp (
  input  [3:0] A,
  output [3:0] R,
  output Overflow
);

  wire fulladder_1_cout, fulladder_2_cout, fulladder_3_cout;
  wire [3:0] onescomp_1_r;

  OnesComp onescomp_1 (.A(A), .R(onescomp_1_r));
  FullAdder fulladder_1 (.A(1'b1), .B(onescomp_1_r[0]), .Sum(R[0]), .Cout(fulladder_1_cout));  // open: Cin
  FullAdder fulladder_2 (.A(onescomp_1_r[1]), .Cin(fulladder_1_cout), .Sum(R[1]), .Cout(fulladder_2_cout));  // open: B
  FullAdder fulladder_3 (.A(onescomp_1_r[2]), .Cin(fulladder_2_cout), .Sum(R[2]), .Cout(fulladder_3_cout));  // open: B
  FullAdder fulladder_4 (.A(onescomp_1_r[3]), .Cin(fulladder_3_cout), .Sum(R[3]), .Cout(Overflow));  // open: B
endmodule

module FourBitAdder (
  input  [3:0] Add1,
  input  [3:0] Add2,
  output [3:0] AddOut
);

  wire fulladder_2_cout, fulladder_3_cout, fulladder_4_cout;

  FullAdder fulladder_1 (.A(Add1[3]), .B(Add2[3]), .Cin(fulladder_2_cout), .Sum(AddOut[3]));  // open: Cout
  FullAdder fulladder_2 (.A(Add1[2]), .B(Add2[2]), .Cin(fulladder_3_cout), .Sum(AddOut[2]), .Cout(fulladder_2_cout));
  FullAdder fulladder_3 (.A(Add1[1]), .B(Add2[1]), .Cin(fulladder_4_cout), .Sum(AddOut[1]), .Cout(fulladder_3_cout));
  FullAdder fulladder_4 (.A(Add1[0]), .B(Add2[0]), .Sum(AddOut[0]), .Cout(fulladder_4_cout));  // open: Cin
endmodule

module FourBitSubtractor (
  input  [3:0] Subtract1,
  input  [3:0] Subtract2,
  output [3:0] SubtractOut
);

  wire fullsubtractor_2_bout, fullsubtractor_3_bout, fullsubtractor_4_bout;

  FullSubtractor fullsubtractor_1 (
    .A(Subtract1[3]), .B(Subtract2[3]), .Bin(fullsubtractor_2_bout), .Sum(SubtractOut[3]));  // open: Bout
  FullSubtractor fullsubtractor_2 (
    .A(Subtract1[2]), .B(Subtract2[2]), .Bin(fullsubtractor_3_bout), .Sum(SubtractOut[2]),
    .Bout(fullsubtractor_2_bout));
  FullSubtractor fullsubtractor_3 (
    .A(Subtract1[1]), .B(Subtract2[1]), .Bin(fullsubtractor_4_bout), .Sum(SubtractOut[1]),
    .Bout(fullsubtractor_3_bout));
  FullSubtractor fullsubtractor_4 (
    .A(Subtract1[0]), .B(Subtract2[0]), .Sum(SubtractOut[0]), .Bout(fullsubtractor_4_bout));  // open: Bin
endmodule

module SR_Latch (
  input  Reset,
  input  Set,
  output Q,
  output NOT_Q
);

  nor nor_1 (Q, Reset, NOT_Q);
  nor nor_2 (NOT_Q, Q, Set);
endmodule

module Clocked_SR_Latch (
  input  Set,
  input  Reset,
  input  Clk,
  output Q,
  output NOT_Q
);

  wire nand_1_out, nand_2_out;

  nand nand_1 (nand_1_out, Set, Clk);
  nand nand_2 (nand_2_out, Clk, Reset);
  nand nand_3 (Q, nand_1_out, NOT_Q);
  nand nand_4 (NOT_Q, Q, nand_2_out);
endmodule

module D_Latch (
  input  D,
  input  Clk,
  output Q,
  output NOT_Q
);

  wire not_1_out;

  not not_1 (not_1_out, D);
  Clocked_SR_Latch clocked_sr_latch_1 (.Set(D), .Reset(not_1_out), .Clk(Clk), .Q(Q), .NOT_Q(NOT_Q));
endmodule

module SR_FlipFlop (
  input  Set,
  input  Reset,
  input  Clk,
  output Q,
  output NOT_Q
);

  wire clocked_sr_latch_1_not_q, clocked_sr_latch_1_q, not_1_out, not_2_out;

  not not_1 (not_1_out, Clk);
  Clocked_SR_Latch clocked_sr_latch_1 (
    .Set(Set), .Reset(Reset), .Clk(not_1_out), .Q(clocked_sr_latch_1_q), .NOT_Q(clocked_sr_latch_1_not_q));
  not not_2 (not_2_out, not_1_out);
  Clocked_SR_Latch clocked_sr_latch_2 (
    .Set(clocked_sr_latch_1_q), .Reset(clocked_sr_latch_1_not_q), .Clk(not_2_out), .Q(Q), .NOT_Q(NOT_Q));

  // Notes on the sheet:
  //   Rising Edge
  //   Falling Edge
endmodule

module D_FlipFlop (
  input  D,
  input  Clk,
  output Q,
  output NOT_Q
);

  wire d_latch_1_not_q, d_latch_1_q, not_1_out, not_2_out;

  not not_1 (not_1_out, Clk);
  D_Latch d_latch_1 (.D(D), .Clk(not_1_out), .Q(d_latch_1_q), .NOT_Q(d_latch_1_not_q));
  not not_2 (not_2_out, not_1_out);
  Clocked_SR_Latch clocked_sr_latch_1 (
    .Set(d_latch_1_q), .Reset(d_latch_1_not_q), .Clk(not_2_out), .Q(Q), .NOT_Q(NOT_Q));

  // Notes on the sheet:
  //   Rising Edge
  //   Falling Edge
endmodule

module JK_FlipFlop (
  input  J,
  input  K,
  input  Clk,
  output Q,
  output NOT_Q
);

  wire and_1_out, and_2_out, not_1_out, or_1_out;

  not not_1 (not_1_out, K);
  and and_1 (and_1_out, NOT_Q, J);
  or or_1 (or_1_out, and_1_out, and_2_out);
  and and_2 (and_2_out, not_1_out, Q);
  D_Flip_Flop d_ff_1 (.D(or_1_out), .clk(Clk), .Q(Q), .Qn(NOT_Q));  // open: preset, reset
endmodule

module T_FlipFlop (
  input  T,
  input  Clk,
  output Q,
  output NOT_Q
);

  wire xor_1_out;

  xor xor_1 (xor_1_out, Q, T);
  D_Flip_Flop d_ff_1 (.D(xor_1_out), .clk(Clk), .Q(Q), .Qn(NOT_Q));  // open: preset, reset
endmodule

module TwoBitRegister (
  input  In0,
  input  In1,
  input  Reset,
  input  Clk,
  output Y0,
  output Y1
);

  D_Flip_Flop d_ff_1 (.D(In0), .clk(Clk), .Q(Y0), .reset(Reset));  // open: Qn, preset
  D_Flip_Flop d_ff_2 (.D(In1), .clk(Clk), .Q(Y1), .reset(Reset));  // open: Qn, preset
endmodule

module FourBitRegister (
  input  In0,
  input  In1,
  input  In2,
  input  In3,
  input  Reset,
  input  Clk,
  output Y0,
  output Y1,
  output Y2,
  output Y3
);

  D_Flip_Flop A0 (.D(In0), .clk(Clk), .Q(Y0), .reset(Reset));  // open: Qn, preset
  D_Flip_Flop A1 (.D(In1), .clk(Clk), .Q(Y1), .reset(Reset));  // open: Qn, preset
  D_Flip_Flop A2 (.D(In2), .clk(Clk), .Q(Y2), .reset(Reset));  // open: Qn, preset
  D_Flip_Flop A3 (.D(In3), .clk(Clk), .Q(Y3), .reset(Reset));  // open: Qn, preset
endmodule

module FourBitRegisterWithLoad (
  input  In0,
  input  In1,
  input  In2,
  input  In3,
  input  Load,
  input  Reset,
  input  Clk,
  output Y0,
  output Y1,
  output Y2,
  output Y3
);

  wire multiplexer_1_out, multiplexer_2_out, multiplexer_3_out, multiplexer_4_out;

  Multiplexer multiplexer_1 (.in0(Y0), .in1(In0), .out(multiplexer_1_out), .sel(Load));
  Multiplexer multiplexer_2 (.in0(Y1), .in1(In1), .out(multiplexer_2_out), .sel(Load));
  Multiplexer multiplexer_3 (.in0(Y2), .in1(In2), .out(multiplexer_3_out), .sel(Load));
  Multiplexer multiplexer_4 (.in0(Y3), .in1(In3), .out(multiplexer_4_out), .sel(Load));
  FourBitRegister fourbitregister_1 (
    .In0(multiplexer_1_out), .In1(multiplexer_2_out), .In2(multiplexer_3_out), .In3(multiplexer_4_out),
    .Reset(Reset), .Clk(Clk), .Y0(Y0), .Y1(Y1), .Y2(Y2), .Y3(Y3));
endmodule

module FourBitRightShiftRegister (
  input  Data_In,
  input  Clk,
  output Out0,
  output Out1,
  output Out2,
  output Out3
);

  D_Flip_Flop d_ff_1 (.D(Data_In), .clk(Clk), .Q(Out3));  // open: Qn, preset, reset
  D_Flip_Flop d_ff_2 (.D(Out3), .clk(Clk), .Q(Out2));  // open: Qn, preset, reset
  D_Flip_Flop d_ff_3 (.D(Out2), .clk(Clk), .Q(Out1));  // open: Qn, preset, reset
  D_Flip_Flop d_ff_4 (.D(Out1), .clk(Clk), .Q(Out0));  // open: Qn, preset, reset
endmodule

module FourBitLeftShiftRegister (
  input  Data_In,
  input  Clk,
  output Out0,
  output Out1,
  output Out2,
  output Out3
);

  D_Flip_Flop d_ff_1 (.D(Out2), .clk(Clk), .Q(Out3));  // open: Qn, preset, reset
  D_Flip_Flop d_ff_2 (.D(Out1), .clk(Clk), .Q(Out2));  // open: Qn, preset, reset
  D_Flip_Flop d_ff_3 (.D(Out0), .clk(Clk), .Q(Out1));  // open: Qn, preset, reset
  D_Flip_Flop d_ff_4 (.D(Data_In), .clk(Clk), .Q(Out0));  // open: Qn, preset, reset
endmodule

module FourBitParallelLoad (
  input  Shift,
  input  Load,
  input  Serial_In,
  input  D0,
  input  D1,
  input  D2,
  input  D3,
  input  Clk,
  output Q0,
  output Q1,
  output Q2,
  output Q3
);

  wire multiplexer_1_out, multiplexer_2_out, multiplexer_3_out, multiplexer_4_out;

  Multiplexer #(.select(2)) multiplexer_1 (
    .in0(Q0), .in1(Serial_In), .in2(D0), .out(multiplexer_1_out), .sel({Load, Shift}));  // open: in3
  Multiplexer #(.select(2)) multiplexer_2 (
    .in0(Q1), .in1(Q0), .in2(D1), .out(multiplexer_2_out), .sel({Load, Shift}));  // open: in3
  Multiplexer #(.select(2)) multiplexer_3 (
    .in0(Q2), .in1(Q1), .in2(D2), .out(multiplexer_3_out), .sel({Load, Shift}));  // open: in3
  Multiplexer #(.select(2)) multiplexer_4 (
    .in0(Q3), .in1(Q2), .in2(D3), .out(multiplexer_4_out), .sel({Load, Shift}));  // open: in3
  D_Flip_Flop d_ff_1 (.D(multiplexer_1_out), .clk(Clk), .Q(Q0));  // open: Qn, preset, reset
  D_Flip_Flop d_ff_2 (.D(multiplexer_2_out), .clk(Clk), .Q(Q1));  // open: Qn, preset, reset
  D_Flip_Flop d_ff_3 (.D(multiplexer_3_out), .clk(Clk), .Q(Q2));  // open: Qn, preset, reset
  D_Flip_Flop d_ff_4 (.D(multiplexer_4_out), .clk(Clk), .Q(Q3));  // open: Qn, preset, reset

  // Notes on the sheet:
  //   Shift = Select_0
  //   Load = Select_1
  //   If Select == 3, unused
  //   If Select == 0, loop the flip-flop back on itself
  //   If Select == 2, put D0, D1, D2, D3 into each register
  //   If Select == 1, output of current the flip-flop goes to the next flip-flop
endmodule
